// Digital circuit ALU.dig as structural Verilog
module ALU (
  input  [7:0] A,
  input  [7:0] B,
  input  SU,
  input  EO,
  output [7:0] out
);

  wire add_2_c_o;
  wire [3:0] add_1_s, add_2_s, xor_1_out;
  wire [7:4] xor_1_out_2;

  assign {xor_1_out_2, xor_1_out} = B ^ {8{SU}};  // XOr xor_1, 8 bits wide
  Add #(.Bits(4)) add_1 (.a(A[7:4]), .b(xor_1_out_2), .c_i(add_2_c_o), .s(add_1_s));  // open: c_o
  Add #(.Bits(4)) add_2 (.a(A[3:0]), .b(xor_1_out), .c_i(SU), .s(add_2_s), .c_o(add_2_c_o));
  assign out = EO ? {add_1_s, add_2_s} : 8'bz;  // Driver driver_1
endmodule
