// Digital circuit uINST.dig as structural Verilog
module uINST (
  input  nclk,
  input  [3:0] OP,
  input  [11:0] ARG,
  input  [2:0] FLAGS,
  output [7:0] DATA,
  output [11:0] ADDR,
  output [12:0] CTRL
);

  wire and_1_out, and_2_out, and_3_out, counter_1_ovf, or_1_out;
  wire [2:0] eeprom_1_d;
  wire [3:0] counter_1_out;

  Counter #(.Bits(4)) counter_1 (.en(1'b1), .C(nclk), .clr(or_1_out), .out(counter_1_out), .ovf(counter_1_ovf));
  or or_1 (or_1_out, eeprom_1_d[2], counter_1_ovf);
  EEPROM #(.AddrBits(11), .Bits(8)) eeprom_1 (
    .A({FLAGS, counter_1_out, OP}), .CS(1'b1), .WE(1'b0), .OE(1'b1), .D({CTRL[4:0], eeprom_1_d}));
  EEPROM #(.AddrBits(11), .Bits(8)) eeprom_2 (
    .A({FLAGS, counter_1_out, OP}), .CS(1'b1), .WE(1'b0), .OE(1'b1), .D(CTRL[12:5]));
  assign DATA = and_1_out ? ARG[7:0] : 8'bz;  // Driver driver_1
  and and_1 (and_1_out, ~eeprom_1_d[1], eeprom_1_d[0]);  // And
  assign ADDR = and_2_out ? ARG : 12'bz;  // Driver driver_2
  and and_2 (and_2_out, eeprom_1_d[1], ~eeprom_1_d[0]);  // And
  assign ADDR = and_3_out ? {ARG[11:4], 4'b0111} : 12'bz;  // Driver driver_3
  and and_3 (and_3_out, eeprom_1_d[1], eeprom_1_d[0]);
endmodule
