// Digital circuit main.dig as structural Verilog
module main (
  input  clk
);

  wire AI, alu_1_p2, AO, BI, BO, BRK, carry, CE, clk_t, DATA, EO, II, J, nand_1_out, nand_2_out, nclk, PO,
       RAO, RBO, reg_a_1_p5, SU, zero;
  wire [10:0] ADDR;
  wire [15:0] IR;

  REG_INST reg_inst_1 (.ii(II), .clk(clk_t), .INST(IR));  // open: ARG, OP
  // PC pc_1: pin names not known; wires that end beside it: ADDR, CE, clk_t, J, PO, ADDR, carry
  EEPROM #(.AddrBits(11), .Bits(8)) ROM_A (.A(ADDR), .CS(1'b1), .WE(1'b0), .OE(1'b1), .D(IR[7:0]));
  EEPROM #(.AddrBits(11), .Bits(8)) ROM_B (.A(ADDR), .CS(1'b1), .WE(1'b0), .OE(1'b1), .D(IR[15:8]));
  assign DATA = RAO ? IR[0] : 1'bz;  // Driver driver_1
  assign DATA = RBO ? IR[8] : 1'bz;  // Driver driver_2
  // REG_A reg_a_1: pin names not known; wires that end beside it: DATA, clk_t, AI, AO, reg_a_1_p5, DATA
  // ALU alu_1: pin names not known; wires that end beside it: reg_a_1_p5, alu_1_p2, SU, EO, DATA, carry, zero
  // REG_B reg_b_1: pin names not known; wires that end beside it: DATA, clk_t, BI, BO, alu_1_p2, DATA
  nand nand_1 (nand_1_out, BRK, BRK);
  nand nand_2 (nand_2_out, nand_1_out, clk);
  nand nand_3 (clk_t, nand_2_out, nand_2_out);
  nand nand_4 (nclk, clk_t, clk_t);
  // Pins of 1 and 8 bits meet at IR[7:0]
  // Pins of 1 and 8 bits meet at IR[15:8]

  // Notes on the sheet:
  //   clk: Hz: 5
endmodule
